// Digital circuit part_c.dig as structural Verilog
module part_c (
  input  in_0,
  input  in_1,
  input  in_2,
  output out_0
);

  wire fgnfet_1_s, fgnfet_3_s, fgnfet_5_s, fgnfet_10_d, fgpfet_1_d, fgpfet_5_d, fgpfet_7_d, fgpfet_8_d,
       fgpfet_9_d, fgpfet_10_d, fgpfet_11_d, undriven, undriven_2, undriven_3, undriven_4;

  FGPFET fgpfet_1 (.G(in_0), .S(1'b1), .D(fgpfet_1_d));
  FGPFET fgpfet_2 (.G(in_0), .S(1'b1));  // open: D
  FGPFET fgpfet_3 (.G(in_1), .S(1'b1));  // open: D
  FGPFET fgpfet_4 (.G(in_2), .S(1'b1), .D(fgpfet_1_d));
  FGNFET fgnfet_1 (.G(in_0), .D(fgpfet_1_d), .S(fgnfet_1_s));
  FGNFET fgnfet_2 (.G(in_2), .D(fgnfet_1_s), .S(1'b0));
  FGPFET fgpfet_5 (.G(in_1), .S(1'b1), .D(fgpfet_5_d));
  FGNFET fgnfet_3 (.G(in_0), .D(fgpfet_5_d), .S(fgnfet_3_s));
  FGNFET fgnfet_4 (.G(in_1), .D(fgnfet_3_s), .S(1'b0));
  FGPFET fgpfet_6 (.G(in_2), .S(1'b1));  // open: D
  FGNFET fgnfet_5 (.G(in_1), .S(fgnfet_5_s));  // open: D
  FGNFET fgnfet_6 (.G(in_2), .D(fgnfet_5_s), .S(1'b0));
  FGPFET fgpfet_7 (.G(undriven), .S(1'b1), .D(fgpfet_7_d));
  FGNFET fgnfet_7 (.G(undriven), .D(fgpfet_7_d), .S(1'b0));
  FGPFET fgpfet_8 (.G(undriven_2), .S(1'b1), .D(fgpfet_8_d));
  FGNFET fgnfet_8 (.G(undriven_2), .D(fgpfet_8_d), .S(1'b0));
  FGPFET fgpfet_9 (.G(undriven_3), .S(1'b1), .D(fgpfet_9_d));
  FGNFET fgnfet_9 (.G(undriven_3), .D(fgpfet_9_d), .S(1'b0));
  FGNFET fgnfet_10 (.G(fgpfet_7_d), .D(fgnfet_10_d), .S(1'b0));
  FGNFET fgnfet_11 (.G(fgpfet_8_d), .D(fgnfet_10_d), .S(1'b0));
  FGPFET fgpfet_10 (.G(fgpfet_7_d), .S(1'b1), .D(fgpfet_10_d));
  FGPFET fgpfet_11 (.G(fgpfet_8_d), .S(fgpfet_10_d), .D(fgpfet_11_d));
  FGPFET fgpfet_12 (.G(fgpfet_9_d), .S(fgpfet_11_d), .D(fgnfet_10_d));
  FGNFET fgnfet_12 (.G(fgpfet_9_d), .D(fgnfet_10_d), .S(1'b0));
  FGPFET fgpfet_13 (.G(undriven_4), .S(1'b1), .D(out_0));
  FGNFET fgnfet_13 (.G(undriven_4), .D(out_0), .S(1'b0));
endmodule

/* Test case part_c_test:
in_0 in_1 in_2 out_0
0 0 0 0
0 0 1 0
0 1 0 0
0 1 1 1
1 0 0 0
1 0 1 1
1 1 0 1
1 1 1 1
*/
