// Digital circuit lab2_part2.dig as structural Verilog
module lab2_part2 (
  input  in0,
  input  in1,
  input  in2,
  input  in3,
  output seg_a,
  output seg_f,
  output seg_b,
  output seg_g,
  output seg_e,
  output seg_c,
  output seg_d,
  output seg_dp,
  output sign_a,
  output sign_f,
  output sign_b,
  output sign_g,
  output sign_e,
  output sign_c,
  output sign_d,
  output sign_dp
);

  wire and_1_out, and_2_out, and_3_out, and_4_out, and_5_out, and_6_out, and_7_out, and_8_out,
       decoder_1_out_0, decoder_1_out_1, decoder_1_out_2, decoder_1_out_3, decoder_1_out_4, decoder_1_out_5,
       decoder_1_out_6, decoder_1_out_7, not_1_out, not_2_out, not_3_out, not_4_out, xor_1_out, xor_3_out,
       xor_4_out, xor_6_out, xor_7_out, xor_9_out, xor_10_out, xor_12_out;
  wire [2:0] xor_2_out;

  Seven_Seg seven_seg_1 (.a(1'b0), .b(1'b0), .c(1'b0), .d(1'b0), .e(1'b0), .f(1'b0), .g(sign_g), .dp(1'b0));
  Seven_Seg seven_seg_2 (.a(seg_a), .b(seg_b), .c(seg_c), .d(seg_d), .e(seg_e), .f(seg_f), .g(seg_g), .dp(seg_dp));
  not not_1 (not_1_out, in0);
  xor xor_1 (xor_1_out, not_1_out, 1'b1);
  xor xor_2 (xor_2_out[0], 1'b0, xor_1_out);
  and and_1 (and_1_out, 1'b1, not_1_out);
  and and_2 (and_2_out, xor_1_out, 1'b0);
  xor xor_3 (xor_3_out, and_1_out, and_2_out);
  not not_2 (not_2_out, in1);
  xor xor_4 (xor_4_out, not_2_out, 1'b0);
  and and_3 (and_3_out, 1'b0, not_2_out);
  and and_4 (and_4_out, xor_4_out, xor_3_out);
  xor xor_5 (xor_2_out[1], xor_3_out, xor_4_out);
  assign seg_a = decoder_1_out_7 ? decoder_1_out_7 : 1'bz;  // Driver driver_1
  Driver driver_2 (.in(decoder_1_out_7), .en(decoder_1_out_7));  // open: out
  Driver driver_3 (.in(decoder_1_out_7), .en(decoder_1_out_7));  // open: out
  Driver driver_4 (.in(decoder_1_out_7), .en(decoder_1_out_7));  // open: out
  Driver driver_5 (.in(decoder_1_out_7), .en(decoder_1_out_7));  // open: out
  Driver driver_6 (.in(decoder_1_out_7), .en(decoder_1_out_7));  // open: out
  Driver driver_7 (.in(decoder_1_out_7), .en(decoder_1_out_7));  // open: out
  xor xor_6 (xor_6_out, and_3_out, and_4_out);
  Driver driver_8 (.in(decoder_1_out_6), .en(decoder_1_out_6));  // open: out
  Driver driver_9 (.in(decoder_1_out_6), .en(decoder_1_out_6));  // open: out
  Driver driver_10 (.in(decoder_1_out_6), .en(decoder_1_out_6));  // open: out
  Driver driver_11 (.in(decoder_1_out_5), .en(decoder_1_out_5));  // open: out
  Driver driver_12 (.in(decoder_1_out_5), .en(decoder_1_out_5));  // open: out
  Driver driver_13 (.in(decoder_1_out_5), .en(decoder_1_out_5));  // open: out
  Driver driver_14 (.in(decoder_1_out_5), .en(decoder_1_out_5));  // open: out
  Driver driver_15 (.in(decoder_1_out_5), .en(decoder_1_out_5));  // open: out
  Driver driver_16 (.in(decoder_1_out_5), .en(decoder_1_out_5));  // open: out
  Driver driver_17 (.in(decoder_1_out_4), .en(decoder_1_out_4));  // open: out
  Driver driver_18 (.in(decoder_1_out_4), .en(decoder_1_out_4));  // open: out
  Driver driver_19 (.in(decoder_1_out_4), .en(decoder_1_out_4));  // open: out
  Driver driver_20 (.in(decoder_1_out_4), .en(decoder_1_out_4));  // open: out
  Driver driver_21 (.in(decoder_1_out_4), .en(decoder_1_out_4));  // open: out
  Driver driver_22 (.in(decoder_1_out_4), .en(decoder_1_out_4));  // open: out
  Driver driver_23 (.in(decoder_1_out_3), .en(decoder_1_out_3));  // open: out
  Driver driver_24 (.in(decoder_1_out_3), .en(decoder_1_out_3));  // open: out
  Driver driver_25 (.in(decoder_1_out_3), .en(decoder_1_out_3));  // open: out
  Driver driver_26 (.in(decoder_1_out_3), .en(decoder_1_out_3));  // open: out
  Driver driver_27 (.in(decoder_1_out_3), .en(decoder_1_out_3));  // open: out
  Decoder #(.Selector_Bits(3)) decoder_1 (
    .sel(xor_2_out), .out_0(decoder_1_out_0), .out_1(decoder_1_out_1), .out_2(decoder_1_out_2),
    .out_3(decoder_1_out_3), .out_4(decoder_1_out_4), .out_5(decoder_1_out_5), .out_6(decoder_1_out_6),
    .out_7(decoder_1_out_7));
  Driver driver_28 (.in(decoder_1_out_0), .en(decoder_1_out_0));  // open: out
  Driver driver_29 (.in(decoder_1_out_0), .en(decoder_1_out_0));  // open: out
  Driver driver_30 (.in(decoder_1_out_0), .en(decoder_1_out_0));  // open: out
  Driver driver_31 (.in(decoder_1_out_0), .en(decoder_1_out_0));  // open: out
  Driver driver_32 (.in(decoder_1_out_1), .en(decoder_1_out_1));  // open: out
  Driver driver_33 (.in(decoder_1_out_1), .en(decoder_1_out_1));  // open: out
  Driver driver_34 (.in(decoder_1_out_1), .en(decoder_1_out_1));  // open: out
  Driver driver_35 (.in(decoder_1_out_1), .en(decoder_1_out_1));  // open: out
  Driver driver_36 (.in(decoder_1_out_1), .en(decoder_1_out_1));  // open: out
  Driver driver_37 (.in(decoder_1_out_1), .en(decoder_1_out_1));  // open: out
  Driver driver_38 (.in(decoder_1_out_2), .en(decoder_1_out_2));  // open: out
  Driver driver_39 (.in(decoder_1_out_2), .en(decoder_1_out_2));  // open: out
  Driver driver_40 (.in(decoder_1_out_2), .en(decoder_1_out_2));  // open: out
  Driver driver_41 (.in(decoder_1_out_2), .en(decoder_1_out_2));  // open: out
  Driver driver_42 (.in(decoder_1_out_2), .en(decoder_1_out_2));  // open: out
  Driver driver_43 (.in(decoder_1_out_2), .en(decoder_1_out_2));  // open: out
  not not_3 (not_3_out, in2);
  xor xor_7 (xor_7_out, not_3_out, 1'b0);
  xor xor_8 (xor_2_out[2], xor_6_out, xor_7_out);
  and and_5 (and_5_out, 1'b0, not_3_out);
  and and_6 (and_6_out, xor_7_out, xor_6_out);
  xor xor_9 (xor_9_out, and_5_out, and_6_out);
  not not_4 (not_4_out, in3);
  xor xor_10 (xor_10_out, not_4_out, 1'b0);
  and and_7 (and_7_out, 1'b0, not_4_out);
  and and_8 (and_8_out, xor_10_out, xor_9_out);
  xor xor_11 (sign_g, xor_9_out, xor_10_out);
  xor xor_12 (xor_12_out, and_7_out, and_8_out);

  assign sign_a = 1'b0;
  assign sign_b = 1'b0;
  assign sign_c = 1'b0;
  assign sign_d = 1'b0;
  assign sign_dp = 1'b0;
  assign sign_e = 1'b0;
  assign sign_f = 1'b0;
  // also tied to GND on the sheet: xor_12_out

  // Notes on the sheet:
  //   Interface (do not edit the content inside this box)
  //   Outputs:
  //   Inputs
  //   Sign
  //   Decimal Number
endmodule

/* Test case:
in3 in2 in1 in0  sign_a sign_b sign_c sign_d sign_e sign_f sign_g  seg_a seg_b seg_c seg_d seg_e seg_f seg_g
 0   0   0   0    0      0      0      0      0      0      0       1     1     1     1     1     1     0
*/
